# Fritzing sketch Boxy_Schematic (saved by Fritzing 0.9.8b)
breadboards: 1

parts:
  HC-SR04_Sensor_1 = HC-SR04 Ultrasonic Distance Sensor
  S1 = Pushbutton [package="[SMD]"]
  R1 = Resistor [tolerance=±5% power=0.25 resistance=10k package=THT]
  Part1 = Breakout Board for Electret Microphone
  Arduino = Arduino Uno (Rev3)

nets (from the breadboard view):
  VCC: HC-SR04_Sensor_1.VCC, S1.Pin_3, S1.Pin_4, R1.Pin_0, R1.Pin_1, Part1.VCC, Arduino.5V
  N1: HC-SR04_Sensor_1.TRIG, Arduino.D9_PWM
  N2: HC-SR04_Sensor_1.ECHO, Arduino.D10_PWM/SS
  GND: HC-SR04_Sensor_1.GND, Part1.GND, Arduino.GND
  N3: S1.Pin_1, S1.Pin_2, Arduino.D8
  N4: Part1.AUD, Arduino.A0
